# Fritzing sketch LED_CIrcuit_DIAGRAM (saved by Fritzing 0.9.3b)
breadboards: 1

parts:
  LED1 = LED - 5mm [color="Red (633nm)" package="5 mm [THT]"]
  R2 = Photocell (LDR) [package=THT]
  R3 = Resistor [tolerance=±5% resistance=220 package=THT]
  R4 = Resistor [tolerance=±5% resistance=220 package=THT]
  Part1 = Arduino Uno (Rev3) - ICSP

nets:
  N1: LED1.cathode, R3.Pin_1
  N2: LED1.anode, Part1.D9_PWM
  N3: R2.pin_0, R4.Pin_1, Part1.A0
  N4: R2.pin_1, R3.Pin_0, Part1.GND
  N5: R4.Pin_0, Part1.5V
